// Logisim project MipsProject-1.circ as structural Verilog: 7 circuits, main circuit main
module main (
  input  Reset,
  input  [7:0] in_2,
  output [7:0] out_3,
  output [3:0] out_4,
  output [7:0] out_5,
  output [3:0] out_6,
  output [7:0] out_7,
  output [7:0] out_8
);

  wire alu_8_by_art_1_p5, Clock_out, controlunit_1_alusrc, controlunit_1_beq, controlunit_1_bneq,
       controlunit_1_jump, controlunit_1_memread, controlunit_1_memtoreg, controlunit_1_memwrite,
       controlunit_1_regdst, controlunit_1_regwrite, multiplexer_2_out;
  wire [2:0] controlunit_1_aluop;
  wire [3:0] instructionmemory_1__7_4_dst, instructionmemory_1__11_8_src2_dst, multiplexer_1_out;
  wire [7:0] adder_1_out, adder_2_out, alu_8_by_art_1_p2, alu_8_by_art_1_p6, bit_extender_1_out,
       datamemory_1_readdata, instructionmemory_1_currentpc, instructionmemory_1_targetjumpaddr,
       multiplexer_3_out, multiplexer_5_out;

  Clock Clock (.out(Clock_out));
  InstructionMemory instructionmemory_1 (
    .NextPC(multiplexer_5_out), .CLK(Clock_out), .Reset(Reset), .Address_Immediate(out_7),
    .CurrentPC(instructionmemory_1_currentpc), ._7_4_Dst(instructionmemory_1__7_4_dst),
    ._11_8_Src2_Dst(instructionmemory_1__11_8_src2_dst), ._15_12_Src_1(out_6), .OpCode(out_4),
    .TargetJumpAddr(instructionmemory_1_targetjumpaddr));  // open: _3_0_Shift
  Adder adder_1 (.a(8'h1), .b(instructionmemory_1_currentpc), .out(adder_1_out));  // open: cin, cout
  Multiplexer #(.width(4), .enable("false")) multiplexer_1 (
    .in0(instructionmemory_1__11_8_src2_dst), .in1(instructionmemory_1__7_4_dst), .out(multiplexer_1_out),
    .sel(controlunit_1_regdst));
  assign bit_extender_1_out = {{4{1'b0}}, instructionmemory_1__7_4_dst};  // Bit_Extender bit_extender_1
  Adder adder_2 (.a(bit_extender_1_out), .b(adder_1_out), .out(adder_2_out));  // open: cin, cout
  ControlUnit controlunit_1 (
    .OpCode(out_4), .ALUOp(controlunit_1_aluop), .Jump(controlunit_1_jump), .bneq(controlunit_1_bneq),
    .beq(controlunit_1_beq), .memwrite(controlunit_1_memwrite), .memread(controlunit_1_memread),
    .regWrite(controlunit_1_regwrite), .memToReg(controlunit_1_memtoreg), .ALUSrc(controlunit_1_alusrc),
    .regDst(controlunit_1_regdst));  // open: Shift
  RegFile regfile_1 (
    .Read_Register_1(out_6), .Read_Register_2(instructionmemory_1__11_8_src2_dst),
    .Write_Register(multiplexer_1_out), .Write_Data(out_5), .Write_Signal(controlunit_1_regwrite),
    .CLK(Clock_out), .Clear(Reset), .Read_Data_1(out_3), .Read_Data_2(out_8));  // open: zero, t0, t1, t2, t3, t4, t5, sp
  Multiplexer multiplexer_2 (
    .in0(controlunit_1_bneq), .in1(controlunit_1_beq), .out(multiplexer_2_out), .sel(alu_8_by_art_1_p5));  // open: en
  Multiplexer #(.width(8), .enable("false")) multiplexer_3 (
    .in0(adder_1_out), .in1(adder_2_out), .out(multiplexer_3_out), .sel(multiplexer_2_out));
  // ALU_8_by_ART alu_8_by_art_1: pin names not known; wires that end beside it: out_3, alu_8_by_art_1_p2, controlunit_1_aluop, alu_8_by_art_1_p2, alu_8_by_art_1_p5, alu_8_by_art_1_p6, in_2
  Multiplexer #(.width(8), .enable("false")) multiplexer_4 (
    .in0(out_8), .in1(out_7), .out(alu_8_by_art_1_p2), .sel(controlunit_1_alusrc));
  Multiplexer #(.width(8), .enable("false")) multiplexer_5 (
    .in0(multiplexer_3_out), .in1(instructionmemory_1_targetjumpaddr), .out(multiplexer_5_out),
    .sel(controlunit_1_jump));
  DataMemory datamemory_1 (
    .Address(alu_8_by_art_1_p6), .WriteData(out_8), .CLK(Clock_out), .CLR(Reset),
    .MemWrite(controlunit_1_memwrite), .MemRead(controlunit_1_memread), .ReadData(datamemory_1_readdata));
  Multiplexer #(.width(8), .enable("false")) multiplexer_6 (
    .in0(alu_8_by_art_1_p6), .in1(datamemory_1_readdata), .out(out_5), .sel(controlunit_1_memtoreg));
endmodule

module RegisterFile (
  input  CLK,
  input  RegWrite,
  input  [3:0] DstReg,
  input  [7:0] WriteData,
  input  CLR,
  input  [3:0] SrcReg1,
  input  [3:0] SrcReg2,
  output [7:0] Read_Data_1,
  output [7:0] Read_Data_2
);

  wire and_1_out, demultiplexer_1_out1, demultiplexer_1_out2, demultiplexer_1_out3, demultiplexer_1_out4,
       demultiplexer_1_out5, demultiplexer_1_out6, not_1_out, not_2_out, not_3_out, not_4_out, not_5_out,
       not_6_out;
  wire [7:0] sp_q, t0_q, t1_q, t2_q, t3_q, t4_q;

  and and_1 (and_1_out, CLK, RegWrite);
  not not_1 (not_1_out, demultiplexer_1_out1);
  Register t0 (.D(WriteData), .Q(t0_q), .clk(not_1_out), .clr(CLR));  // open: en
  Demultiplexer #(.select(3), .enable("false")) demultiplexer_1 (
    .out1(demultiplexer_1_out1), .out2(demultiplexer_1_out2), .out3(demultiplexer_1_out3),
    .out4(demultiplexer_1_out4), .out5(demultiplexer_1_out5), .out6(demultiplexer_1_out6), .in(and_1_out),
    .sel(DstReg[2:0]));  // open: out0, out7
  not not_2 (not_2_out, demultiplexer_1_out2);
  Register t1 (.D(WriteData), .Q(t1_q), .clk(not_2_out), .clr(CLR));  // open: en
  not not_3 (not_3_out, demultiplexer_1_out3);
  Register t2 (.D(WriteData), .Q(t2_q), .clk(not_3_out), .clr(CLR));  // open: en
  Multiplexer #(.select(3), .width(8), .enable("false")) multiplexer_1 (
    .in0({8{1'b0}}), .in1(t0_q), .in2(t1_q), .in3(t2_q), .in4(t3_q), .in5(t4_q), .in6(sp_q), .in7({8{1'b0}}),
    .out(Read_Data_1), .sel(SrcReg1[2:0]));
  Multiplexer #(.select(3), .width(8), .enable("false")) multiplexer_2 (
    .in0({8{1'b0}}), .in1(t0_q), .in2(t1_q), .in3(t2_q), .in4(t3_q), .in5(t4_q), .in6(sp_q), .in7({8{1'b0}}),
    .out(Read_Data_2), .sel(SrcReg2[2:0]));
  not not_4 (not_4_out, demultiplexer_1_out4);
  Register t3 (.D(WriteData), .Q(t3_q), .clk(not_4_out), .clr(CLR));  // open: en
  not not_5 (not_5_out, demultiplexer_1_out5);
  Register t4 (.D(WriteData), .Q(t4_q), .clk(not_5_out), .clr(CLR));  // open: en
  not not_6 (not_6_out, demultiplexer_1_out6);
  Register sp (.D(WriteData), .Q(sp_q), .clk(not_6_out), .clr(CLR));  // open: en

  // Notes on the sheet:
  //   $zero
endmodule

module InstructionMemory (
  input  [7:0] NextPC,
  input  CLK,
  input  Reset,
  output [7:0] Address_Immediate,
  output [7:0] CurrentPC,
  output [3:0] _3_0_Shift,
  output [3:0] _7_4_Dst,
  output [3:0] _11_8_Src2_Dst,
  output [3:0] _15_12_Src_1,
  output [3:0] OpCode,
  output [7:0] TargetJumpAddr
);

  Register PC (.D(NextPC), .Q(CurrentPC), .clk(CLK), .clr(Reset));  // open: en
  ROM #(.dataWidth(20)) rom_1 (
    .addr(CurrentPC), .data({OpCode, _15_12_Src_1, _11_8_Src2_Dst, _7_4_Dst, _3_0_Shift}), .sel(1'b1));

  assign Address_Immediate = {_7_4_Dst, _3_0_Shift};
  assign TargetJumpAddr = {_15_12_Src_1, _11_8_Src2_Dst};

  // Notes on the sheet:
  //   contents of rom_1 (hex, n*v repeats v):
  //   20a 305 e2310 e1340 e4150 f3203 82201 d2401 a1500 b5150 12202 34401 43203 62410 c1530 a1400 51105
  //   23314 93330 a1500 713fb
endmodule

module ControlUnit (
  input  [3:0] OpCode,
  output [2:0] ALUOp,
  output Shift,
  output Jump,
  output bneq,
  output beq,
  output memwrite,
  output memread,
  output regWrite,
  output memToReg,
  output ALUSrc,
  output regDst
);

  ROM #(.addrWidth(4), .dataWidth(13)) rom_1 (
    .addr(OpCode),
    .data({regDst, ALUSrc, memToReg, regWrite, memread, memwrite, beq, bneq, Jump, Shift, ALUOp}));  // open: sel

  // Notes on the sheet:
  //   contents of rom_1 (hex, n*v repeats v):
  //   a00 a01 a03 a0e f00 a02 1203 21 a0d 1204 10 1201 1202 41 1200 c80
endmodule

module DataMemory (
  input  [7:0] Address,
  input  [7:0] WriteData,
  input  CLK,
  input  CLR,
  input  MemWrite,
  input  MemRead,
  output [7:0] ReadData
);

  wire not_1_out;

  not not_1 (not_1_out, CLK);
  RAM #(.bus("separate")) ram_1 (
    .addr(Address), .din(WriteData), .data(ReadData), .str(MemWrite), .clk(not_1_out), .ld(MemRead), .clr(CLR));  // open: sel
endmodule

module RegFile (
  input  [3:0] Read_Register_1,
  input  [3:0] Read_Register_2,
  input  [3:0] Write_Register,
  input  [7:0] Write_Data,
  input  Write_Signal,
  input  CLK,
  input  Clear,
  output [7:0] Read_Data_1,
  output [7:0] Read_Data_2,
  output [7:0] sp,
  output [7:0] zero,
  output [7:0] t5,
  output [7:0] t0,
  output [7:0] t4,
  output [7:0] t1,
  output [7:0] t2,
  output [7:0] t3
);

  wire and_1_out, and_2_out, and_3_out, and_4_out, and_5_out, and_6_out, and_7_out, and_8_out,
       decoder_1_out0, decoder_1_out1, decoder_1_out2, decoder_1_out3, decoder_1_out4, decoder_1_out5,
       decoder_1_out6, decoder_1_out7, multiplexer_1_out, multiplexer_3_out;
  wire [7:0] multiplexer_2_out;

  Decoder #(.select(4), .enable("false")) decoder_1 (
    .out0(decoder_1_out0), .out1(decoder_1_out1), .out2(decoder_1_out2), .out3(decoder_1_out3),
    .out4(decoder_1_out4), .out5(decoder_1_out5), .out6(decoder_1_out6), .out7(decoder_1_out7),
    .sel(Write_Register));  // open: out8, out9, out10, out11, out12, out13, out14, out15
  and and_1 (and_1_out, decoder_1_out0, 1'b0);
  and and_2 (and_2_out, decoder_1_out1, Write_Signal);
  and and_3 (and_3_out, decoder_1_out2, Write_Signal);
  and and_4 (and_4_out, decoder_1_out3, Write_Signal);
  and and_5 (and_5_out, decoder_1_out4, Write_Signal);
  and and_6 (and_6_out, decoder_1_out5, Write_Signal);
  and and_7 (and_7_out, decoder_1_out6, Write_Signal);
  and and_8 (and_8_out, decoder_1_out7, Write_Signal);
  Multiplexer #(.enable("false")) multiplexer_1 (.in0(and_8_out), .in1(Clear), .out(multiplexer_1_out), .sel(Clear));
  Multiplexer #(.width(8), .enable("false")) multiplexer_2 (
    .in0(Write_Data), .in1({8{1'b1}}), .out(multiplexer_2_out), .sel(Clear));
  Register u_zero (.D(Write_Data), .en(and_1_out), .Q(zero), .clk(CLK), .clr(Clear));
  Register u_t0 (.D(Write_Data), .en(and_2_out), .Q(t0), .clk(CLK), .clr(Clear));
  Register u_t1 (.D(Write_Data), .en(and_3_out), .Q(t1), .clk(CLK), .clr(Clear));
  Register u_t2 (.D(Write_Data), .en(and_4_out), .Q(t2), .clk(CLK), .clr(Clear));
  Register u_t3 (.D(Write_Data), .en(and_5_out), .Q(t3), .clk(CLK), .clr(Clear));
  Register u_t4 (.D(Write_Data), .en(and_6_out), .Q(t4), .clk(CLK), .clr(Clear));
  Register u_t5 (.D(Write_Data), .en(and_7_out), .Q(t5), .clk(CLK), .clr(Clear));
  Register u_sp (.D(multiplexer_2_out), .en(multiplexer_1_out), .Q(sp), .clk(multiplexer_3_out));  // open: clr
  Multiplexer #(.enable("false")) multiplexer_3 (.in0(CLK), .in1(Clear), .out(multiplexer_3_out), .sel(Clear));
  Multiplexer #(.select(4), .width(8), .enable("false")) multiplexer_4 (
    .in0(zero), .in1(t0), .in2(t1), .in3(t2), .in4(t3), .in5(t4), .in6(t5), .in7(sp), .out(Read_Data_1),
    .sel(Read_Register_1));  // open: in8, in9, in10, in11, in12, in13, in14, in15
  Multiplexer #(.select(4), .width(8), .enable("false")) multiplexer_5 (
    .in0(zero), .in1(t0), .in2(t1), .in3(t2), .in4(t3), .in5(t4), .in6(t5), .in7(sp), .out(Read_Data_2),
    .sel(Read_Register_2));  // open: in8, in9, in10, in11, in12, in13, in14, in15
endmodule

module main1 (
  input  Reset,
  output [7:0] out_2,
  output [3:0] out_3,
  output [3:0] out_4,
  output [7:0] out_5
);

  wire alu_8_by_art_1_p4, Clock_out, controlunit_1_alusrc, controlunit_1_beq, controlunit_1_bneq,
       controlunit_1_jump, controlunit_1_memread, controlunit_1_memtoreg, controlunit_1_memwrite,
       controlunit_1_regdst, controlunit_1_regwrite, controlunit_1_shift, multiplexer_3_out;
  wire [2:0] controlunit_1_aluop;
  wire [3:0] instructionmemory_1__3_0_shift, instructionmemory_1__7_4_dst,
       instructionmemory_1__11_8_src2_dst, multiplexer_1_out, multiplexer_2_out;
  wire [7:0] adder_1_out, adder_2_out, alu_8_by_art_1_p2, alu_8_by_art_1_p5, datamemory_1_readdata,
       instructionmemory_1_address_immediate, instructionmemory_1_currentpc,
       instructionmemory_1_targetjumpaddr, multiplexer_4_out, multiplexer_5_out, multiplexer_6_out,
       multiplexer_8_out, regfile_1_read_data_1;

  Clock Clock (.out(Clock_out));
  InstructionMemory instructionmemory_1 (
    .NextPC(multiplexer_8_out), .CLK(Clock_out), .Reset(Reset),
    .Address_Immediate(instructionmemory_1_address_immediate), .CurrentPC(instructionmemory_1_currentpc),
    ._3_0_Shift(instructionmemory_1__3_0_shift), ._7_4_Dst(instructionmemory_1__7_4_dst),
    ._11_8_Src2_Dst(instructionmemory_1__11_8_src2_dst), ._15_12_Src_1(out_3), .OpCode(out_4),
    .TargetJumpAddr(instructionmemory_1_targetjumpaddr));
  Adder adder_1 (.a(8'h1), .b(instructionmemory_1_currentpc), .out(adder_1_out));  // open: cin, cout
  Multiplexer #(.width(4), .enable("false")) multiplexer_1 (
    .in0(instructionmemory_1__11_8_src2_dst), .in1(instructionmemory_1__7_4_dst), .out(multiplexer_1_out),
    .sel(controlunit_1_regdst));
  Multiplexer #(.width(4), .enable("false")) multiplexer_2 (
    .in0(instructionmemory_1__7_4_dst), .in1(4'b0000), .out(multiplexer_2_out), .sel(controlunit_1_shift));
  Adder adder_2 (.a(instructionmemory_1_address_immediate), .b(adder_1_out), .out(adder_2_out));  // open: cin, cout
  ControlUnit controlunit_1 (
    .OpCode(out_4), .ALUOp(controlunit_1_aluop), .Shift(controlunit_1_shift), .Jump(controlunit_1_jump),
    .bneq(controlunit_1_bneq), .beq(controlunit_1_beq), .memwrite(controlunit_1_memwrite),
    .memread(controlunit_1_memread), .regWrite(controlunit_1_regwrite), .memToReg(controlunit_1_memtoreg),
    .ALUSrc(controlunit_1_alusrc), .regDst(controlunit_1_regdst));
  RegFile regfile_1 (
    .Read_Register_1(out_3), .Read_Register_2(instructionmemory_1__11_8_src2_dst),
    .Write_Register(multiplexer_1_out), .Write_Data(out_2), .Write_Signal(controlunit_1_regwrite),
    .CLK(Clock_out), .Clear(Reset), .Read_Data_1(regfile_1_read_data_1), .Read_Data_2(out_5));  // open: zero, t0, t1, t2, t3, t4, t5, sp
  Multiplexer multiplexer_3 (
    .in0(controlunit_1_bneq), .in1(controlunit_1_beq), .out(multiplexer_3_out), .sel(alu_8_by_art_1_p4));  // open: en
  Multiplexer #(.width(8), .enable("false")) multiplexer_4 (
    .in0(regfile_1_read_data_1), .in1(multiplexer_5_out), .out(multiplexer_4_out), .sel(controlunit_1_shift));
  Multiplexer #(.width(8), .enable("false")) multiplexer_5 (
    .in0(out_5), .in1({multiplexer_2_out, instructionmemory_1__3_0_shift}), .out(multiplexer_5_out),
    .sel(controlunit_1_alusrc));
  Multiplexer #(.width(8), .enable("false")) multiplexer_6 (
    .in0(adder_1_out), .in1(adder_2_out), .out(multiplexer_6_out), .sel(multiplexer_3_out));
  // ALU_8_by_ART alu_8_by_art_1: pin names not known; wires that end beside it: multiplexer_4_out, alu_8_by_art_1_p2, controlunit_1_aluop, alu_8_by_art_1_p4, alu_8_by_art_1_p5
  Multiplexer #(.width(8), .enable("false")) multiplexer_7 (
    .in0(multiplexer_5_out), .in1(regfile_1_read_data_1), .out(alu_8_by_art_1_p2), .sel(controlunit_1_shift));
  Multiplexer #(.width(8), .enable("false")) multiplexer_8 (
    .in0(multiplexer_6_out), .in1(instructionmemory_1_targetjumpaddr), .out(multiplexer_8_out),
    .sel(controlunit_1_jump));
  DataMemory datamemory_1 (
    .Address(alu_8_by_art_1_p5), .WriteData(out_5), .CLK(Clock_out), .CLR(Reset),
    .MemWrite(controlunit_1_memwrite), .MemRead(controlunit_1_memread), .ReadData(datamemory_1_readdata));
  Multiplexer #(.width(8), .enable("false")) multiplexer_9 (
    .in0(alu_8_by_art_1_p5), .in1(datamemory_1_readdata), .out(out_2), .sel(controlunit_1_memtoreg));
endmodule
